// Logisim project Lab_2_Solutions.circ as structural Verilog: 13 circuits, main circuit main
module main (
  input  v3,
  input  v2,
  input  v1,
  input  v0
);

  wire circuit_b_1_o0, circuit_b_1_o1, circuit_b_1_o2, multiplexer_1_out, multiplexer_2_out,
       multiplexer_3_out, multiplexer_4_out, s0, s1, s2, s3, s4, s5, s6, s7, s8, s9, s10, s11, s12, s13, z;
  wire [6:0] seg7_decoder_1_o_seg;

  Circuit_b circuit_b_1 (.v2(v2), .v1(v1), .v0(v0), .o2(circuit_b_1_o2), .o1(circuit_b_1_o1), .o0(circuit_b_1_o0));
  comp comp_1 (.v3(v3), .v2(v2), .v1(v1), .v0(v0), .z(z));
  Multiplexer multiplexer_1 (.in0(v3), .out(multiplexer_1_out), .sel(1'b0));  // open: in1
  Multiplexer multiplexer_2 (.in0(v2), .in1(circuit_b_1_o2), .out(multiplexer_2_out), .sel(z));
  Multiplexer multiplexer_3 (.in0(v1), .in1(circuit_b_1_o1), .out(multiplexer_3_out), .sel(z));
  Multiplexer multiplexer_4 (.in0(v0), .in1(circuit_b_1_o0), .out(multiplexer_4_out), .sel(z));
  Circuit_a circuit_a_1 (.z(z), .s6(s13), .s5(s12), .s4(s11), .s3(s10), .s2(s9), .s1(s8), .s0(s7));
  Seg7_Decoder seg7_decoder_1 (
    .i_m3(multiplexer_1_out), .i_m2(multiplexer_2_out), .i_m1(multiplexer_3_out), .i_m0(multiplexer_4_out),
    .o_seg(seg7_decoder_1_o_seg));
  not not_1 (s0, seg7_decoder_1_o_seg[0]);
  not not_2 (s1, seg7_decoder_1_o_seg[1]);
  not not_3 (s2, seg7_decoder_1_o_seg[2]);
  not not_4 (s3, seg7_decoder_1_o_seg[3]);
  not not_5 (s4, seg7_decoder_1_o_seg[4]);
  not not_6 (s5, seg7_decoder_1_o_seg[5]);
  not not_7 (s6, seg7_decoder_1_o_seg[6]);
  _7_Segment_Display u_7_segment_display_1 (.g(s13), .f(s12), .a(s7), .b(s8), .e(s11), .d(s10), .c(s9));  // open: dp
  _7_Segment_Display u_7_segment_display_2 (.g(s6), .f(s5), .a(s0), .b(s1), .e(s4), .d(s3), .c(s2));  // open: dp
endmodule

module Seg7_Decoder (
  input  i_m3,
  input  i_m2,
  input  i_m1,
  input  i_m0,
  output [6:0] o_seg
);

  wire and_1_out, and_2_out, and_3_out, and_4_out, and_5_out, and_6_out, and_7_out, and_8_out, and_9_out,
       and_10_out, and_12_out, and_13_out, and_14_out, and_15_out, not_1_out, not_2_out, not_3_out, not_4_out;

  not not_1 (not_1_out, i_m3);
  not not_2 (not_2_out, i_m2);
  not not_3 (not_3_out, i_m1);
  not not_4 (not_4_out, i_m0);
  and and_1 (and_1_out, not_1_out, not_2_out, not_3_out);
  and and_2 (and_2_out, i_m2, i_m1, i_m0);
  and and_3 (and_3_out, i_m3, not_2_out, i_m1, not_4_out);
  and and_4 (and_4_out, not_1_out, not_2_out, i_m0);
  and and_5 (and_5_out, not_1_out, not_2_out, i_m1);
  and and_6 (and_6_out, i_m1, i_m0);
  and and_7 (and_7_out, i_m2, not_3_out);
  and and_8 (and_8_out, not_1_out, not_2_out, not_3_out, i_m0);
  and and_9 (and_9_out, i_m2, not_3_out, not_4_out);
  and and_10 (and_10_out, i_m2, i_m1, i_m0);
  and and_11 (o_seg[2], not_1_out, not_2_out, i_m1, not_4_out);
  and and_12 (and_12_out, i_m2, not_3_out, i_m0);
  and and_13 (and_13_out, i_m2, i_m1, not_4_out);
  and and_14 (and_14_out, not_1_out, not_2_out, not_3_out, i_m0);
  and and_15 (and_15_out, i_m2, not_3_out, not_4_out);
  or or_1 (o_seg[6], and_1_out, and_2_out, and_3_out);
  or or_2 (o_seg[5], and_4_out, and_5_out, and_6_out);
  or or_3 (o_seg[4], i_m0, and_7_out);
  or or_4 (o_seg[3], and_8_out, and_9_out, and_10_out);
  or or_5 (o_seg[1], and_12_out, and_13_out);
  or or_6 (o_seg[0], and_14_out, and_15_out);
endmodule

module Circuit_b (
  input  v2,
  input  v1,
  input  v0,
  output o2,
  output o1,
  output o0
);

  not not_1 (o1, v1);
  and and_1 (o2, v2, v1);

  assign o0 = v0;
endmodule

module comp (
  input  v3,
  input  v2,
  input  v1,
  input  v0,
  output z
);

  wire and_1_out, and_2_out;

  and and_1 (and_1_out, v3, v1);
  and and_2 (and_2_out, v3, v2);
  or or_1 (z, and_1_out, and_2_out);
endmodule

module Circuit_a (
  input  z,
  output s6,
  output s5,
  output s4,
  output s3,
  output s2,
  output s1,
  output s0
);


  assign s0 = 1'b0;
  assign s1 = z;
  assign s2 = z;
  assign s3 = 1'b0;
  assign s4 = 1'b0;
  assign s5 = 1'b0;
  assign s6 = 1'b0;
endmodule

module full_adder (
  input  c_i,
  input  a,
  input  b,
  output s,
  output c_o
);

  wire xor_1_out;

  xor xor_1 (xor_1_out, a, b);
  Multiplexer multiplexer_1 (.in0(b), .in1(c_i), .out(c_o), .sel(xor_1_out));
  xor xor_2 (s, c_i, xor_1_out);
endmodule

module rip_carry_adder_4bit (
  input  c_i,
  input  a0,
  input  b0,
  input  a1,
  input  b1,
  input  a2,
  input  b2,
  input  a3,
  input  b3,
  output s0,
  output s1,
  output s2,
  output s3,
  output c_o
);

  wire c1, c2, c3;

  full_adder fa0 (.c_i(c_i), .a(a0), .b(b0), .s(s0), .c_o(c1));
  full_adder fa1 (.c_i(c1), .a(a1), .b(b1), .s(s1), .c_o(c2));
  full_adder fa2 (.c_i(c2), .a(a2), .b(b2), .s(s2), .c_o(c3));
  full_adder fa3 (.c_i(c3), .a(a3), .b(b3), .s(s3), .c_o(c_o));
endmodule

module Part_3 (
  input  c_i,
  input  a3,
  input  a2,
  input  a1,
  input  a0,
  input  b3,
  input  b2,
  input  b1,
  input  b0
);

  wire o0, o1, o2, o3, rip_carry_adder_4bit_1_c_o, s0, s1, s2, s3, s4, s5, s6;
  wire [6:0] seg7_decoder_1_o_seg;

  rip_carry_adder_4bit rip_carry_adder_4bit_1 (
    .c_i(c_i), .a0(a0), .b0(b0), .a1(a1), .b1(b1), .a2(a2), .b2(b2), .a3(a3), .b3(b3), .s0(o0), .s1(o1),
    .s2(o2), .s3(o3), .c_o(rip_carry_adder_4bit_1_c_o));
  Seg7_Decoder seg7_decoder_1 (.i_m3(o3), .i_m2(o2), .i_m1(o1), .i_m0(o0), .o_seg(seg7_decoder_1_o_seg));
  LED led_1 (.in(rip_carry_adder_4bit_1_c_o));
  not not_1 (s0, seg7_decoder_1_o_seg[0]);
  not not_2 (s1, seg7_decoder_1_o_seg[1]);
  not not_3 (s2, seg7_decoder_1_o_seg[2]);
  not not_4 (s3, seg7_decoder_1_o_seg[3]);
  not not_5 (s4, seg7_decoder_1_o_seg[4]);
  not not_6 (s5, seg7_decoder_1_o_seg[5]);
  not not_7 (s6, seg7_decoder_1_o_seg[6]);
  _7_Segment_Display u_7_segment_display_1 (.g(s6), .f(s5), .a(s0), .b(s1), .e(s4), .d(s3), .c(s2));  // open: dp
endmodule

module Comp4 (
  input  sum0,
  input  sum1,
  input  sum2,
  input  sum3,
  input  carry,
  output z
);

  wire and_1_out, and_2_out;

  and and_1 (and_1_out, sum2, sum3);
  and and_2 (and_2_out, sum1, sum3);
  or or_1 (z, and_1_out, carry, and_2_out);

  // Other names for the same wires on the sheet: c = carry; s0 = sum0; s1 = sum1; s2 = sum2; s3 = sum3
endmodule

module Circuit_b4 (
  input  sum0,
  input  sum1,
  input  sum2,
  input  sum3,
  input  carry,
  output a_o0,
  output a_o1,
  output a_o2,
  output a_o3
);

  wire and_1_out, and_2_out, not_1_out;

  not not_1 (not_1_out, sum1);
  and and_1 (and_1_out, not_1_out, carry);
  and and_2 (and_2_out, sum1, sum2, sum3);
  not not_2 (a_o1, sum1);
  or or_1 (a_o2, and_1_out, and_2_out);
  and and_3 (a_o3, sum1, carry);

  assign a_o0 = sum0;

  // Other names for the same wires on the sheet: c = carry; s0 = sum0; s1 = sum1; s2 = sum2; s3 = sum3
endmodule

module Part_4 (
  input  c_i,
  input  a3,
  input  a2,
  input  a1,
  input  a0,
  input  b3,
  input  b2,
  input  b1,
  input  b0
);

  wire a_o0, a_o1, a_o2, a_o3, c, o0, o1, o2, o3, s0, S0_0, S0_1, S0_2, S0_3, s1, s2, s3, s4, s5, s6, s7, s8,
       s9, s10, s11, s12, s13, z;
  wire [6:0] Dec_S0_o_seg, Dec_S1_o_seg;

  Seg7_Decoder Dec_S0 (.i_m3(S0_3), .i_m2(S0_2), .i_m1(S0_1), .i_m0(S0_0), .o_seg(Dec_S0_o_seg));
  Seg7_Decoder Dec_S1 (.i_m3(1'b0), .i_m2(1'b0), .i_m1(1'b0), .i_m0(z), .o_seg(Dec_S1_o_seg));
  not not_1 (s0, Dec_S0_o_seg[0]);
  not not_2 (s1, Dec_S0_o_seg[1]);
  not not_3 (s2, Dec_S0_o_seg[2]);
  not not_4 (s3, Dec_S0_o_seg[3]);
  not not_5 (s4, Dec_S0_o_seg[4]);
  not not_6 (s5, Dec_S0_o_seg[5]);
  not not_7 (s6, Dec_S0_o_seg[6]);
  not not_8 (s13, Dec_S1_o_seg[0]);
  not not_9 (s12, Dec_S1_o_seg[1]);
  not not_10 (s11, Dec_S1_o_seg[2]);
  not not_11 (s10, Dec_S1_o_seg[3]);
  not not_12 (s9, Dec_S1_o_seg[4]);
  not not_13 (s8, Dec_S1_o_seg[5]);
  not not_14 (s7, Dec_S1_o_seg[6]);
  rip_carry_adder_4bit rip_carry_adder_4bit_1 (
    .c_i(c_i), .a0(a0), .b0(b0), .a1(a1), .b1(b1), .a2(a2), .b2(b2), .a3(a3), .b3(b3), .s0(o0), .s1(o1),
    .s2(o2), .s3(o3), .c_o(c));
  Comp4 comp4_1 (.sum0(o0), .sum1(o1), .sum2(o2), .sum3(o3), .carry(c), .z(z));
  Circuit_b4 circuit_b4_1 (
    .sum0(o0), .sum1(o1), .sum2(o2), .sum3(o3), .carry(c), .a_o0(a_o0), .a_o1(a_o1), .a_o2(a_o2), .a_o3(a_o3));
  Multiplexer multiplexer_1 (.in0(o0), .in1(a_o0), .out(S0_0), .sel(z));
  Multiplexer multiplexer_2 (.in0(o1), .in1(a_o1), .out(S0_1), .sel(z));
  Multiplexer multiplexer_3 (.in0(o2), .in1(a_o2), .out(S0_2), .sel(z));
  Multiplexer multiplexer_4 (.in0(o3), .in1(a_o3), .out(S0_3), .sel(z));
  _7_Segment_Display u_7_segment_display_1 (.g(s7), .f(s8), .a(s13), .b(s12), .e(s9), .d(s10), .c(s11));  // open: dp
  _7_Segment_Display u_7_segment_display_2 (.g(s6), .f(s5), .a(s0), .b(s1), .e(s4), .d(s3), .c(s2));  // open: dp
endmodule

module bcd_adder (
  input  c_i,
  input  a3,
  input  a2,
  input  a1,
  input  a0,
  input  b3,
  input  b2,
  input  b1,
  input  b0,
  output S0,
  output S1,
  output S2,
  output S3,
  output c_o
);

  wire a_o0, a_o1, a_o2, a_o3, c, o0, o1, o2, o3;

  rip_carry_adder_4bit rip_carry_adder_4bit_1 (
    .c_i(c_i), .a0(a0), .b0(b0), .a1(a1), .b1(b1), .a2(a2), .b2(b2), .a3(a3), .b3(b3), .s0(o0), .s1(o1),
    .s2(o2), .s3(o3), .c_o(c));
  Comp4 comp4_1 (.sum0(o0), .sum1(o1), .sum2(o2), .sum3(o3), .carry(c), .z(c_o));
  Circuit_b4 circuit_b4_1 (
    .sum0(o0), .sum1(o1), .sum2(o2), .sum3(o3), .carry(c), .a_o0(a_o0), .a_o1(a_o1), .a_o2(a_o2), .a_o3(a_o3));
  Multiplexer multiplexer_1 (.in0(o0), .in1(a_o0), .out(S0), .sel(c_o));
  Multiplexer multiplexer_2 (.in0(o1), .in1(a_o1), .out(S1), .sel(c_o));
  Multiplexer multiplexer_3 (.in0(o2), .in1(a_o2), .out(S2), .sel(c_o));
  Multiplexer multiplexer_4 (.in0(o3), .in1(a_o3), .out(S3), .sel(c_o));

  // Other names for the same wires on the sheet: z = c_o
endmodule

module Part_5 (
  input  [3:0] A0,
  input  [3:0] B0,
  input  [3:0] A1,
  input  [3:0] B1
);

  wire c1, h0, h1, h2, h3, h4, h5, h6, s0, S0_0, S0_1, S0_2, S0_3, s1, S1_0, S1_1, S1_2, S1_3, S2, s2_t, s3,
       s4, s5, s6, s7, s8, s9, s10, s11, s12, s13;
  wire [6:0] Dec_S0_o_seg, Dec_S1_o_seg, seg7_decoder_1_o_seg;

  _7_Segment_Display u_7_segment_display_1 (.g(h6), .f(h5), .a(h0), .b(h1), .e(h4), .d(h3), .c(h2));  // open: dp
  _7_Segment_Display u_7_segment_display_2 (.g(s7), .f(s8), .a(s13), .b(s12), .e(s9), .d(s10), .c(s11));  // open: dp
  _7_Segment_Display u_7_segment_display_3 (.g(s6), .f(s5), .a(s0), .b(s1), .e(s4), .d(s3), .c(s2_t));  // open: dp
  bcd_adder bcd1 (
    .c_i(c1), .a3(A1[3]), .a2(A1[2]), .a1(A1[1]), .a0(A1[0]), .b3(B1[3]), .b2(B1[2]), .b1(B1[1]), .b0(B1[0]),
    .S0(S1_0), .S1(S1_1), .S2(S1_2), .S3(S1_3), .c_o(S2));
  bcd_adder bcd0 (
    .c_i(1'b0), .a3(A0[3]), .a2(A0[2]), .a1(A0[1]), .a0(A0[0]), .b3(B0[3]), .b2(B0[2]), .b1(B0[1]),
    .b0(B0[0]), .S0(S0_0), .S1(S0_1), .S2(S0_2), .S3(S0_3), .c_o(c1));
  Seg7_Decoder Dec_S0 (.i_m3(S0_3), .i_m2(S0_2), .i_m1(S0_1), .i_m0(S0_0), .o_seg(Dec_S0_o_seg));
  Seg7_Decoder Dec_S1 (.i_m3(S1_3), .i_m2(S1_2), .i_m1(S1_1), .i_m0(S1_0), .o_seg(Dec_S1_o_seg));
  Seg7_Decoder seg7_decoder_1 (.i_m3(1'b0), .i_m2(1'b0), .i_m1(1'b0), .i_m0(S2), .o_seg(seg7_decoder_1_o_seg));
  not not_1 (s0, Dec_S0_o_seg[0]);
  not not_2 (s1, Dec_S0_o_seg[1]);
  not not_3 (s2_t, Dec_S0_o_seg[2]);
  not not_4 (s3, Dec_S0_o_seg[3]);
  not not_5 (s4, Dec_S0_o_seg[4]);
  not not_6 (s5, Dec_S0_o_seg[5]);
  not not_7 (s6, Dec_S0_o_seg[6]);
  not not_8 (s13, Dec_S1_o_seg[0]);
  not not_9 (s12, Dec_S1_o_seg[1]);
  not not_10 (s11, Dec_S1_o_seg[2]);
  not not_11 (s10, Dec_S1_o_seg[3]);
  not not_12 (s9, Dec_S1_o_seg[4]);
  not not_13 (s8, Dec_S1_o_seg[5]);
  not not_14 (s7, Dec_S1_o_seg[6]);
  not not_15 (h0, seg7_decoder_1_o_seg[0]);
  not not_16 (h1, seg7_decoder_1_o_seg[1]);
  not not_17 (h2, seg7_decoder_1_o_seg[2]);
  not not_18 (h3, seg7_decoder_1_o_seg[3]);
  not not_19 (h4, seg7_decoder_1_o_seg[4]);
  not not_20 (h5, seg7_decoder_1_o_seg[5]);
  not not_21 (h6, seg7_decoder_1_o_seg[6]);

  // Other names for the same wires on the sheet: a0_0 = A0[0]; a0_1 = A0[1]; a0_2 = A0[2]; a0_3 = A0[3]; a1_0 = A1[0];
  //   a1_1 = A1[1]; a1_2 = A1[2]; a1_3 = A1[3]; b0_0 = B0[0]; b0_1 = B0[1]; b0_2 = B0[2]; b0_3 = B0[3]; b1_0 = B1[0];
  //   b1_1 = B1[1]; b1_2 = B1[2]; b1_3 = B1[3]
endmodule
