// Logisim project Simulations.circ as structural Verilog: 5 circuits, main circuit main
module main (
);

  wire button_1_out, multiplexer_1_out;

  Button button_1 (.out(button_1_out));
  Multiplexer multiplexer_1 (.out(multiplexer_1_out), .sel(button_1_out));  // open: in0, in1
  D_L_Dff d_l_dff_1 (.D(multiplexer_1_out));  // open: clk, Q_a, Q_b
  D_ff d_ff_1 ();  // open: D, Q, Q_n
endmodule

module D_L (
  input  D,
  output Q_a,
  output Q_b
);

  wire clk_out, nand_1_out, nand_2_out, not_1_out;

  Clock clk (.out(clk_out));
  not not_1 (not_1_out, D);
  nand nand_1 (nand_1_out, D, clk_out);
  nand nand_2 (nand_2_out, clk_out, not_1_out);
  nand nand_3 (Q_a, nand_1_out, Q_b);
  nand nand_4 (Q_b, Q_a, nand_2_out);
endmodule

module RS_L (
  input  R,
  input  S,
  output Q_a,
  output Q_b
);

  wire and_1_out, and_2_out, clk_out;

  Clock clk (.out(clk_out));
  and and_1 (and_1_out, R, clk_out);
  and and_2 (and_2_out, clk_out, S);
  nor nor_1 (Q_a, and_1_out, Q_b);
  nor nor_2 (Q_b, Q_a, and_2_out);
endmodule

module D_ff (
  input  D,
  output Q,
  output Q_n
);

  wire clk_out, lead_q_a, not_1_out;

  Clock clk (.out(clk_out));
  not not_1 (not_1_out, clk_out);
  D_L_Dff lead (.D(D), .clk(not_1_out), .Q_a(lead_q_a));  // open: Q_b
  D_L_Dff tail (.D(lead_q_a), .clk(clk_out), .Q_a(Q), .Q_b(Q_n));
endmodule

module D_L_Dff (
  input  D,
  input  clk,
  output Q_a,
  output Q_b
);

  wire nand_1_out, nand_2_out, not_1_out;

  not not_1 (not_1_out, D);
  nand nand_1 (nand_1_out, D, clk);
  nand nand_2 (nand_2_out, clk, not_1_out);
  nand nand_3 (Q_a, nand_1_out, Q_b);
  nand nand_4 (Q_b, Q_a, nand_2_out);
endmodule
