// Logisim project simulations.circ as structural Verilog
module d_ff (
  input  D,
  input  Clk,
  output Q,
  output Q_n
);

  wire d_l_1_q_a, not_1_out;

  not not_1 (not_1_out, Clk);
  d_L d_l_1 (.D(D), .clk(not_1_out), .Q_a(d_l_1_q_a));  // open: Q_b
  d_L d_l_2 (.D(d_l_1_q_a), .clk(Clk), .Q_a(Q), .Q_b(Q_n));
endmodule

module d_L (
  input  D,
  input  clk,
  output Q_a,
  output Q_b
);

  wire nand_1_out, nand_2_out, not_1_out;

  not not_1 (not_1_out, D);
  nand nand_1 (nand_1_out, D, clk);
  nand nand_2 (nand_2_out, clk, not_1_out);
  nand nand_3 (Q_a, nand_1_out, Q_b);
  nand nand_4 (Q_b, Q_a, nand_2_out);
endmodule

module T_ff (
  input  T,
  input  Clear,
  input  Clk,
  output Q,
  output out_5
);

  wire and_1_out, and_2_out, multiplexer_1_out, not_1_out, not_2_out, or_1_out;

  not not_1 (not_1_out, T);
  not not_2 (not_2_out, Q);
  and and_1 (and_1_out, not_1_out, Q);
  and and_2 (and_2_out, not_2_out, T);
  or or_1 (or_1_out, and_1_out, and_2_out);
  Multiplexer multiplexer_1 (.in0(or_1_out), .in1(1'b0), .out(multiplexer_1_out), .sel(Clear));
  d_ff d_ff_1 (.D(multiplexer_1_out), .Clk(Clk), .Q(Q), .Q_n(out_5));
endmodule

module bit8_counter (
  input  Enable,
  input  Clear
);

  wire clk, q0, q1, q2, q3, q4, q5, q6, q7, s0, s1, s2, s3, s4, s5, s6, s7, s8, s9, s10, s11, s12, s13, t0,
       t1, t2, t3, t4, t5, t6, t7;
  wire [6:0] seg7_decoder_1_o_seg, seg7_decoder_2_o_seg;

  _7_Segment_Display u_7_segment_display_1 (.g(s7), .f(s8), .a(s13), .b(s12), .e(s9), .d(s10), .c(s11));  // open: dp
  Clock #(.highDuration(50), .lowDuration(50)) C (.out(clk));
  _7_Segment_Display u_7_segment_display_2 (.g(s6), .f(s5), .a(s0), .b(s1), .e(s4), .d(s3), .c(s2));  // open: dp
  T_ff t_ff_1 (.T(Enable), .Clear(Clear), .Clk(clk), .Q(q0));  // open: out_5
  T_ff t_ff_2 (.T(t0), .Clear(Clear), .Clk(clk), .Q(q1));  // open: out_5
  T_ff t_ff_3 (.T(t1), .Clear(Clear), .Clk(clk), .Q(q2));  // open: out_5
  T_ff t_ff_4 (.T(t2), .Clear(Clear), .Clk(clk), .Q(q3));  // open: out_5
  and and_1 (t0, Enable, q0);
  and and_2 (t1, t0, q1);
  and and_3 (t2, t1, q2);
  and and_4 (t3, t2, q3);
  T_ff t_ff_5 (.T(t3), .Clear(Clear), .Clk(clk), .Q(q4));  // open: out_5
  T_ff t_ff_6 (.T(t4), .Clear(Clear), .Clk(clk), .Q(q5));  // open: out_5
  T_ff t_ff_7 (.T(t5), .Clear(Clear), .Clk(clk), .Q(q6));  // open: out_5
  T_ff t_ff_8 (.T(t6), .Clear(Clear), .Clk(clk), .Q(q7));  // open: out_5
  and and_5 (t4, t3, q4);
  and and_6 (t5, t4, q5);
  and and_7 (t6, t5, q6);
  and and_8 (t7, t6, q7);
  seg7_decoder seg7_decoder_1 (.i_m3(q3), .i_m2(q2), .i_m1(q1), .i_m0(q0), .o_seg(seg7_decoder_1_o_seg));
  seg7_decoder seg7_decoder_2 (.i_m3(q7), .i_m2(q6), .i_m1(q5), .i_m0(q4), .o_seg(seg7_decoder_2_o_seg));
  not not_1 (s0, seg7_decoder_1_o_seg[0]);
  not not_2 (s1, seg7_decoder_1_o_seg[1]);
  not not_3 (s2, seg7_decoder_1_o_seg[2]);
  not not_4 (s3, seg7_decoder_1_o_seg[3]);
  not not_5 (s4, seg7_decoder_1_o_seg[4]);
  not not_6 (s5, seg7_decoder_1_o_seg[5]);
  not not_7 (s6, seg7_decoder_1_o_seg[6]);
  not not_8 (s13, seg7_decoder_2_o_seg[0]);
  not not_9 (s12, seg7_decoder_2_o_seg[1]);
  not not_10 (s11, seg7_decoder_2_o_seg[2]);
  not not_11 (s10, seg7_decoder_2_o_seg[3]);
  not not_12 (s9, seg7_decoder_2_o_seg[4]);
  not not_13 (s8, seg7_decoder_2_o_seg[5]);
  not not_14 (s7, seg7_decoder_2_o_seg[6]);

  // Other names for the same wires on the sheet: clr = Clear; ena = Enable
endmodule

module seg7_decoder (
  input  i_m3,
  input  i_m2,
  input  i_m1,
  input  i_m0,
  output [6:0] o_seg
);

  wire and_1_out, and_2_out, and_3_out, and_4_out, and_5_out, and_6_out, and_7_out, and_8_out, and_9_out,
       and_10_out, and_11_out, and_12_out, and_13_out, and_14_out, and_15_out, and_16_out, and_17_out,
       and_18_out, and_19_out, and_20_out, and_21_out, and_22_out, and_23_out, and_24_out, and_25_out,
       not_1_out, not_2_out, not_3_out, not_4_out;

  not not_1 (not_1_out, i_m3);
  not not_2 (not_2_out, i_m2);
  not not_3 (not_3_out, i_m1);
  not not_4 (not_4_out, i_m0);
  and and_1 (and_1_out, not_1_out, not_2_out, not_3_out);
  and and_2 (and_2_out, not_1_out, i_m2, i_m1, i_m0);
  and and_3 (and_3_out, i_m3, i_m2, not_3_out, not_4_out);
  and and_4 (and_4_out, not_1_out, not_2_out, i_m0);
  and and_5 (and_5_out, not_1_out, not_2_out, i_m1);
  and and_6 (and_6_out, not_1_out, i_m1, i_m0);
  and and_7 (and_7_out, i_m3, i_m2, not_3_out, i_m0);
  and and_8 (and_8_out, not_1_out, i_m0);
  and and_9 (and_9_out, not_1_out, i_m2, not_3_out);
  and and_10 (and_10_out, not_2_out, not_3_out, i_m0);
  and and_11 (and_11_out, not_1_out, not_2_out, not_3_out, i_m0);
  and and_12 (and_12_out, not_1_out, i_m2, not_3_out, not_4_out);
  and and_13 (and_13_out, i_m2, i_m1, i_m0);
  and and_14 (and_14_out, i_m3, not_2_out, i_m1, not_4_out);
  and and_15 (and_15_out, not_1_out, not_2_out, i_m1, not_4_out);
  and and_16 (and_16_out, i_m3, i_m2, not_4_out);
  and and_17 (and_17_out, i_m3, i_m2, i_m1);
  and and_18 (and_18_out, not_1_out, i_m2, not_3_out, i_m0);
  and and_19 (and_19_out, i_m2, i_m1, not_4_out);
  and and_20 (and_20_out, i_m3, i_m1, i_m0);
  and and_21 (and_21_out, i_m3, i_m2, not_4_out);
  and and_22 (and_22_out, not_1_out, not_2_out, not_3_out, i_m0);
  and and_23 (and_23_out, not_1_out, i_m2, not_3_out, not_4_out);
  and and_24 (and_24_out, i_m3, not_2_out, i_m1, i_m0);
  and and_25 (and_25_out, i_m3, i_m2, not_3_out, i_m0);
  or or_1 (o_seg[6], and_1_out, and_2_out, and_3_out);
  or or_2 (o_seg[5], and_4_out, and_5_out, and_6_out, and_7_out);
  or or_3 (o_seg[4], and_8_out, and_9_out, and_10_out);
  or or_4 (o_seg[3], and_11_out, and_12_out, and_13_out, and_14_out);
  or or_5 (o_seg[2], and_15_out, and_16_out, and_17_out);
  or or_6 (o_seg[1], and_18_out, and_19_out, and_20_out, and_21_out);
  or or_7 (o_seg[0], and_22_out, and_23_out, and_24_out, and_25_out);
endmodule
